# Fritzing sketch licenta (saved by Fritzing 0.9.4)
breadboards: 1

parts:
  U1 = BATTERY-2 [package=battery-aaa]
  U2 = BATTERY-2 [package=battery-aaa]
  U3 = BATTERY-2 [package=battery-aaa]
  U4 = BATTERY-2 [package=battery-aaa]
  INA1 = INA219 DC Current Sensor Breakout
  INA2 = INA219 DC Current Sensor Breakout
  Part1 = Arduino Uno (Rev3)
  M3 = Getriebemotor
  M4 = Getriebemotor
  M5 = Getriebemotor
  M6 = Getriebemotor
  Q1 = Basic FET P-Channel [package="TO220 [THT]"]
  L298N1 = L298N DC motor driver

nets:
  N1: U1.-2, U2.-2
  N2: U1.+2, U2.+2
  GND: U2.-1, INA1.GND, INA1.Vin-2, INA2.GND, Part1.GND, Q1.gate
  N3: U2.+1, U4.-1, INA1.Vin+2, INA2.Vin-2
  N4: U3.-2, U4.-2
  N5: U3.+2, U4.+2
  N6: U4.+1, INA2.Vin+2, Part1.VIN, Q1.drain, Q1.source
  VCC: INA1.VCC, INA2.VCC, Part1.5V
  N7: INA1.SCL, Part1.A0
  N8: INA1.SDA, Part1.A1
  N9: INA2.SCL, Part1.A2
  N10: INA2.SDA, Part1.A3
  N11: M3.pin_1, M4.pin_1, L298N1.OUT4
  N12: M3.pin_2, M4.pin_2, L298N1.OUT3
  N13: M5.pin_1, M6.pin_1, L298N1.OUT2
  N14: M5.pin_2, M6.pin_2, L298N1.OUT1

custom parts:
  INA219 DC Current Sensor Breakout: INA DC Current Sensor Breakout
  L298N DC motor driver: 2x DC motor driver with 78M05 positive voltage regulator (7..35 V) L298N: max 46 V, 2 A Set 5 V Enable jumper to enable 5 V regultor (needed for the L298N) and +5 V output at screw terminal or supply external +5 V at screw terminal Set ENA and/or ENB to +5 V to enable motor permanently or supply ENA and/or ENB with PWM signal IN1 and IN2 set rotation directory for motor A (OUT1/OUT2) IN2 and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

// code stored in the sketch: getcurrent.ino
#include <Wire.h>
#include <Adafruit_INA219.h>

Adafruit_INA219 ina219;


void setup(void) 
{
  Serial.begin(115200);
  while (!Serial) {
      // will pause Zero, Leonardo, etc until serial console opens
      delay(1);
  }
    
  Serial.println("Hello!");
  
  // Initialize the INA219.
  // By default the initialization will use the largest range (32V, 2A).  However
  // you can call a setCalibration function to change this range (see comments).
  if (! ina219.begin()) {
    Serial.println("Failed to find INA219 chip");
    while (1) { delay(10); }
  }
  // To use a slightly lower 32V, 1A range (higher precision on amps):
  //ina219.setCalibration_32V_1A();
  // Or to use a lower 16V, 400mA range (higher precision on volts and amps):
  //ina219.setCalibration_16V_400mA();

  Serial.println("Measuring voltage and current with INA219 ...");
}

void loop(void) 
{
  float shuntvoltage = 0;
  float busvoltage = 0;
  float current_mA = 0;
  float loadvoltage = 0;
  float power_mW = 0;

  shuntvoltage = ina219.getShuntVoltage_mV();
  busvoltage = ina219.getBusVoltage_V();
  current_mA = ina219.getCurrent_mA();
  power_mW = ina219.getPower_mW();
  loadvoltage = busvoltage + (shuntvoltage / 1000);
  
  Serial.print("Bus Voltage:   "); Serial.print(busvoltage); Serial.println(" V");
  Serial.print("Shunt Voltage: "); Serial.print(shuntvoltage); Serial.println(" mV");
  Serial.print("Load Voltage:  "); Serial.print(loadvoltage); Serial.println(" V");
  Serial.print("Current:       "); Serial.print(current_mA); Serial.println(" mA");
  Serial.print("Power:         "); Serial.print(power_mW); Serial.println(" mW");
  Serial.println("");

  delay(2000);
}
